# Fritzing sketch Arduino_Mega_Hub (saved by Fritzing 1.0.2b)
breadboards: 1

parts:
  Bauteil1 = Arduino Mega 2560 (Rev3)
  Bauteil2 = LCD1602-I2C
  M1 = Osoyoo SX1278-ra-02
  ANT1 = Antenna  # not connected

nets:
  N1: Bauteil1.D21/SCL, Bauteil2.SCL
  N2: Bauteil1.D20/SDA, Bauteil2.SDA
  N3: Bauteil1.D10_PWM, M1.NSS
  N4: Bauteil1.D9_PWM, M1.RST
  3V3: Bauteil1.3V3, M1.3.3V
  5V: Bauteil1.5V, Bauteil2.VCC
  GND: Bauteil1.GND, Bauteil2.GND, M1.GND
  N5: Bauteil1.D50, M1.MISO
  N6: Bauteil1.D51, M1.MOSI
  N7: Bauteil1.D52, M1.SCK

notes:
  5.5V

custom parts:
  LCD1602-I2C: A standard character display, usually with 2x16 characters. Comes in many colors with LCM1602 IIC attached.
  Osoyoo SX1278-ra-02: Osoyoo Long Distance wireless transceiver Uart LoRa Module.
